# Fritzing sketch Colour Sensor Wearable (saved by Fritzing 0.9.4)
breadboards: 1

parts:
  U1 = atmega328 [package=dip]
  Part1 = Color Sensor Breakout ADJD-S311  # not connected
  BAT1 = Battery Holders [package=battcon_245mm_pth]
  S1 = SWITCH-MOMENTARY-2 [package=tactile-pth-12mm]
  S2 = SWITCH-MOMENTARY-2 [package=tactile-pth-12mm]
  LED3 = LED_RING [package=led_ring]
  R1 = Resistor [tolerance=±5% resistance=220 package="2010 [SMD]"]
  R2 = Resistor [tolerance=±5% resistance=220 package="2010 [SMD]"]
  R3 = Resistor [tolerance=±5% resistance=220 package="2010 [SMD]"]
  R4 = Resistor [tolerance=±5% resistance=220 package="2010 [SMD]"]
  R5 = Resistor [tolerance=±5% resistance=220 package="2010 [SMD]"]
  R6 = Resistor [tolerance=±5% resistance=220 package="2010 [SMD]"]
  R7 = Resistor [tolerance=±5% resistance=220 package="2010 [SMD]"]
  R8 = Resistor [tolerance=±5% resistance=220 package="2010 [SMD]"]
  XTAL1 = Crystal [frequency="16 Mhz" package=SMD]
  U2 = Vibration Motor- ROB-08449 [package=vibe-motor-10mm]

nets:
  N1: U1.D2, U2.-
  N2: U1.D3_(PWM), S2.2
  N3: U1.VCC, U1.AVCC, U1.AREF, S1.1
  N4: U1.GND, BAT1.-, S2.1, LED3.COM0, U2.+
  N5: U1.XLAT1, XTAL1.pin_0
  N6: U1.XLAT2, XTAL1.pin_1
  N7: U1.D6_(PWM), R3.Pin_0
  N8: U1.D7, R4.Pin_0
  N9: U1.D8, R2.Pin_0
  N10: U1.D9_(PWM), R5.Pin_0
  N11: U1.D10_(PWM), R8.Pin_0
  N12: U1.D11_(PWM), R6.Pin_0
  N13: U1.D12, R7.Pin_0
  N14: U1.D13, R1.Pin_0
  N15: BAT1.+, S1.2
  N16: LED3.1, R8.Pin_1
  N17: LED3.2, R6.Pin_1
  N18: LED3.3, R7.Pin_1
  N19: LED3.4, R1.Pin_1
  N20: LED3.13, R3.Pin_1
  N21: LED3.14, R4.Pin_1
  N22: LED3.15, R2.Pin_1
  N23: LED3.16, R5.Pin_1
